# Fritzing sketch KeyBug_recup (saved by Fritzing 0.7.10b)
stripboards: 1

parts:
  S4 = Pushbutton [package="[SMD]"]
  R4 = Resistor [tolerance=±5% resistance=1k package="0805 [SMD]"]
  C10 = Ceramic Capacitor [capacitance=22pF package="0805 [SMD, multilayer]"]
  C11 = Ceramic Capacitor [capacitance=22pF package="0805 [SMD, multilayer]"]
  C12 = Ceramic Capacitor [capacitance=100nF package="0805 [SMD, multilayer]"]
  ICSP = female pin header, 6 pins [form="♀ (female rounded)"]
  XTAL3 = Crystal [frequency="16 Mhz" package=SMD]
  U6 = atmega168 [package="DIP28 [THT]"]
  Bluetooth = female pin header, 4 pins [form="♀ (female)"]
  U7 = mystery part, 4 pins [chip_label=Usb]
  D1 = Zener Diode [part_number=1N4732A breakdown_voltage=3.6V package="300 mil [THT]"]
  D2 = Zener Diode [part_number=1N4732A breakdown_voltage=3.6V package="300 mil [THT]"]
  R5 = Resistor [tolerance=±5% resistance=268 package=THT]
  R6 = Resistor [tolerance=±5% resistance=268 package=THT]
  R7 = Resistor [tolerance=±5% resistance=2.2k package=THT]

nets (from the schematic view):
  N1: S4.Pin_1, S4.Pin_2, R4.Pin_0, C12.1, U6.Pin_1
  GND: S4.Pin_3, S4.Pin_4, C10.0, C11.1, ICSP.pin5, ICSP.pin6, U6.Pin_8, U6.Pin_22, U7.pin4, D1.anode, D2.anode
  5V: R4.Pin_1, ICSP.pin4, U6.Pin_7, U6.Pin_20, U6.Pin_21, Bluetooth.pin1, U7.pin1
  N2: C10.1, XTAL3.pin_0, U6.Pin_9
  N3: C11.0, XTAL3.pin_1, U6.Pin_10
  N4: C12.0, ICSP.pin1
  N5: ICSP.pin2, U6.Pin_3, Bluetooth.pin4
  N6: ICSP.pin3, U6.Pin_2, Bluetooth.pin3
  N7: U6.Pin_4, R5.Pin_1
  N8: U6.Pin_6, R6.Pin_1
  N9: U6.Pin_11, R7.Pin_0
  N10: U7.pin2, D2.cathode, R5.Pin_0, R6.Pin_0, R7.Pin_1
  N11: U7.pin3, D1.cathode
